# Fritzing sketch drumlights (saved by Fritzing 0.9.0b)
breadboards: 1

parts:
  TRINKET1 = Trinket 5V
  J1 = Piezo Speaker
  R1 = Resistor [tolerance=±20% resistance=1M package=THT]
  Power_plug1 = Power plug
  NEOPIXEL1 = Neopixel Strip -- Black (60/m)
  C1 = Electrolytic Capacitor [capacitance=1µF package="100 mil [THT, electrolytic]"]

nets:
  VCC: TRINKET1.no_name_yet#1, Power_plug1.VCC, NEOPIXEL1.+5V, C1.+
  GND: TRINKET1.no_name_yet#2, J1.pin2, R1.Pin_1, Power_plug1.GND, NEOPIXEL1.GND, C1.-
  N1: TRINKET1.no_name_yet#7, J1.pin1, R1.Pin_0
  N2: TRINKET1.no_name_yet#9, NEOPIXEL1.DI

custom parts:
  Trinket 5V: Adafruit Trinket 5V
  Neopixel Strip -- Black (60/m): Neopixel Strip, Black, 60 pixels per meter.
